# Fritzing sketch nodoTanqueAgua (saved by Fritzing 0.9.6b)

parts:
  HC-SR04_Sensor_1 = HC-SR04 Ultrasonic Distance Sensor
  HLK-PM1 = HLK-PM01
  WeMos_D1_Mini1 = WeMos D1 Mini
  LED1 = smd LED [color="Red (633nm)" package="0805 [SMD]"]
  LED2 = smd LED [color="White (4500K)" package="0805 [SMD]"]
  LED3 = smd LED [color="Yellow (595nm)" package="0805 [SMD]"]
  LED4 = smd LED [color="Blue (525nm)" package="0805 [SMD]"]
  R1 = Resistor [tolerance=±5% resistance=330 package="1206 [SMD]"]
  R2 = Resistor [tolerance=±5% resistance=330 package="1206 [SMD]"]
  R3 = Resistor [tolerance=±5% resistance=330 package="1206 [SMD]"]
  R4 = Resistor [tolerance=±5% resistance=330 package="1206 [SMD]"]

nets:
  VCC: HC-SR04_Sensor_1.VCC, HLK-PM1.+Vo, WeMos_D1_Mini1.5V
  N1: HC-SR04_Sensor_1.TRIG, WeMos_D1_Mini1.D3
  N2: HC-SR04_Sensor_1.ECHO, WeMos_D1_Mini1.D4
  N3: HC-SR04_Sensor_1.GND, HLK-PM1.-Vo, WeMos_D1_Mini1.G, LED1.cathode, LED2.cathode, LED3.cathode, LED4.cathode
  N4: WeMos_D1_Mini1.D0, R1.Pin_1
  N5: WeMos_D1_Mini1.D5, R2.Pin_1
  N6: WeMos_D1_Mini1.D6, R3.Pin_1
  N7: WeMos_D1_Mini1.D7, R4.Pin_1

// code stored in the sketch: nodoTanqueAgua.ino
int trig = D3;
int echo = D4;
//int signal = 11;
int blanco = D0;
int amarillo = D5;
int azul = D6;
int rojo = D7;
int duracion;
int distancia;
  
void setup()
{
  pinMode(trig, OUTPUT);  
  pinMode(echo, INPUT);
  pinMode(blanco, OUTPUT);
  pinMode(amarillo, OUTPUT);
  pinMode(azul, OUTPUT);
  pinMode(rojo, OUTPUT);
  Serial.begin(9600);
}

void loop()
{
  digitalWrite (trig, HIGH);
  delay(1);
  digitalWrite (trig, LOW);
  duracion = pulseIn(echo, HIGH);
  distancia = duracion / 58.2;
  //distancia /= 100;
  
  if (distancia <= 100){
    digitalWrite(blanco, HIGH);
    digitalWrite(amarillo, LOW);
    digitalWrite(azul, LOW);
    digitalWrite(rojo, LOW);
      Serial.println("Tanque lleno");
  } else if (distancia <= 150){
    digitalWrite(blanco, LOW);
    digitalWrite(amarillo, HIGH);
    digitalWrite(azul, LOW);
    digitalWrite(rojo, LOW);
      Serial.println("Tanque a la mitad");
  } else if (distancia <= 200){
    digitalWrite(blanco, LOW);
    digitalWrite(amarillo, LOW);
    digitalWrite(azul, HIGH);
    digitalWrite(rojo, LOW);    
      Serial.println("Tanque a 1/4");
  } else {
    digitalWrite(blanco, LOW);
    digitalWrite(amarillo, LOW);
    digitalWrite(azul, LOW);
    digitalWrite(rojo, HIGH);
      Serial.println("Tanque vacio");
  }
  delay(200);
}
